// Digital circuit uart.dig as structural Verilog
module uart (
  input  clk,
  input  rx,
  input  interrupt_accept,
  input  assert_main,
  input  [15:0] main_bus_2,
  input  read_main,
  output [3:0] interrupt_bus,
  output interrupt_request,
  output [15:0] main_bus,
  output tx
);

  wire _7400_1_pin2, _74165_1_pin9, c_0, c_1, c_2, c_3, d_ff_1_q, le, not_1_out, not_3_out, not_4_out, q_0,
       q_1, q_2, q_3, q_4, q_5, q_6, q_7, read, reading, start_tx, uart_clk;

  not not_1 (not_1_out, read);
  D_FF d_ff_1 (.D(read), .C(uart_clk), .Q(d_ff_1_q));  // open: nQ
  not not_2 (read, read_main);
  nand nand_1 (start_tx, not_1_out, d_ff_1_q);
  _74163 _74163_1 (
    .pin1(1'b1), .pin2(clk), .pin3(1'b0), .pin4(1'b0), .pin5(1'b0), .pin6(1'b0), .pin7(1'b1), .pin8(1'b0),
    .pin9(1'b1), .pin10(1'b1), .pin11(uart_clk), .pin16(1'b1));  // open: pin12, pin13, pin14, pin15
  _7400 _7400_1 (
    .pin1(rx), .pin2(_7400_1_pin2), .pin3(reading), .pin4(reading), .pin5(q_7), .pin6(_7400_1_pin2),
    .pin7(1'b0), .pin9(1'b1), .pin10(1'b1), .pin12(1'b1), .pin13(1'b1), .pin14(1'b1));  // open: pin8, pin11
  _74164 _74164_1 (
    .pin1(1'b1), .pin2(rx), .pin3(q_0), .pin4(q_1), .pin5(q_2), .pin6(q_3), .pin7(1'b0), .pin8(uart_clk),
    .pin9(1'b1), .pin10(q_4), .pin11(q_5), .pin12(q_6), .pin13(q_7), .pin14(1'b1));
  _74165 _74165_1 (
    .pin1(start_tx), .pin2(uart_clk), .pin3(1'b1), .pin4(1'b1), .pin5(1'b1), .pin6(main_bus_2[7]),
    .pin8(1'b0), .pin9(_74165_1_pin9), .pin10(1'b1), .pin11(1'b1), .pin12(1'b1), .pin13(1'b1), .pin14(1'b1),
    .pin15(1'b0), .pin16(1'b1));  // open: pin7
  not not_3 (not_3_out, le);
  not not_4 (not_4_out, assert_main);
  _74163 _74163_2 (
    .pin1(not_3_out), .pin2(uart_clk), .pin3(1'b0), .pin4(1'b0), .pin5(1'b0), .pin6(1'b0), .pin7(reading),
    .pin8(1'b0), .pin9(1'b1), .pin10(1'b1), .pin11(c_3), .pin12(c_2), .pin13(c_1), .pin14(c_0), .pin16(1'b1));  // open: pin15
  _74373 _74373_1 (
    .pin1(not_4_out), .pin2(main_bus[0]), .pin3(q_0), .pin4(q_1), .pin5(main_bus[1]), .pin6(main_bus[2]),
    .pin7(q_2), .pin8(q_3), .pin9(main_bus[3]), .pin10(1'b0), .pin11(le), .pin12(main_bus[4]), .pin13(q_4),
    .pin14(q_5), .pin15(main_bus[5]), .pin16(main_bus[6]), .pin17(q_6), .pin18(q_7), .pin19(main_bus[7]),
    .pin20(1'b1));
  _74165 _74165_2 (
    .pin1(start_tx), .pin2(uart_clk), .pin3(main_bus_2[2]), .pin4(main_bus_2[1]), .pin5(main_bus_2[0]),
    .pin6(1'b0), .pin8(1'b0), .pin9(tx), .pin10(_74165_1_pin9), .pin11(main_bus_2[6]), .pin12(main_bus_2[5]),
    .pin13(main_bus_2[4]), .pin14(main_bus_2[3]), .pin15(1'b0), .pin16(1'b1));  // open: pin7
  and and_1 (le, ~c_0, ~c_1, ~c_2, c_3);  // And
  RS_FF_AS rs_ff_as_1 (.S(le), .R(interrupt_accept), .Q(interrupt_request));  // open: nQ

  assign interrupt_bus = 4'b0001;
  assign main_bus[15:8] = {8{1'b0}};

  // Other names for the same wires on the sheet: assert = assert_main; d_0 = main_bus[0]; d_1 = main_bus[1];
  //   d_2 = main_bus[2]; d_3 = main_bus[3]; d_4 = main_bus[4]; d_5 = main_bus[5]; d_6 = main_bus[6];
  //   d_7 = main_bus[7]; int_acc = interrupt_accept; main_0 = main_bus_2[0]; main_1 = main_bus_2[1];
  //   main_2 = main_bus_2[2]; main_3 = main_bus_2[3]; main_4 = main_bus_2[4]; main_5 = main_bus_2[5];
  //   main_6 = main_bus_2[6]; main_7 = main_bus_2[7]; rst_rx = q_7

  // Notes on the sheet:
  //   clk: Hz: 16
  //   rx: default 1
endmodule
